// Logisim project hw3.circ as structural Verilog: 5 circuits, main circuit SR_Latch
module SR_Latch (
  input  in_1,
  input  in_2,
  output out_3,
  output out_4
);

  wire or_1_out, or_2_out;

  or or_1 (or_1_out, in_1, out_4);
  or or_2 (or_2_out, out_3, in_2);
  not not_1 (out_3, or_1_out);
  not not_2 (out_4, or_2_out);

  // Notes on the sheet:
  //   Provided for you
endmodule

module D_Latch (
  input  in_1,
  input  in_2,
  output out_3
);

  wire and_1_out, and_2_out, not_1_out;

  not not_1 (not_1_out, in_1);
  and and_1 (and_1_out, in_1, in_2);
  and and_2 (and_2_out, not_1_out, in_2);
  SR_Latch SR (.in_1(and_1_out), .in_2(and_2_out), .out_4(out_3));  // open: out_3

  // Notes on the sheet:
  //   Strobe
  //   Provided for you
  //   We ignore the NOT Q output
endmodule

module Decoder (
  input  in_1,
  input  in_2,
  output out_3,
  output out_4,
  output out_5,
  output out_6
);

  wire not_1_out, not_2_out, not_3_out, not_4_out;

  not not_1 (not_1_out, in_1);
  not not_2 (not_2_out, in_2);
  not not_3 (not_3_out, in_1);
  not not_4 (not_4_out, in_2);
  and and_1 (out_3, not_1_out, not_2_out);
  and and_2 (out_4, not_3_out, in_2);
  and and_3 (out_5, in_1, not_4_out);
  and and_4 (out_6, in_1, in_2);

  // Notes on the sheet:
  //   Provided for you
endmodule

module RAM (
  input  in_1,
  input  _2Bit_Addr,
  input  in_3,
  input  _3Bit_Data,
  input  in_5,
  input  Write,
  output out_7,
  output _3_Bit_Out,
  output out_9
);

  wire and_1_out, and_2_out, and_3_out, and_4_out, d_latch_1_out_3, d_latch_2_out_3, d_latch_3_out_3,
       d_latch_4_out_3, d_latch_5_out_3, d_latch_6_out_3, d_latch_7_out_3, d_latch_8_out_3, d_latch_9_out_3,
       d_latch_10_out_3, d_latch_11_out_3, d_latch_12_out_3, decoder_1_out_3, decoder_1_out_4,
       decoder_1_out_5, decoder_1_out_6;

  Decoder decoder_1 (
    .out_4(decoder_1_out_4), .out_6(decoder_1_out_6), .out_5(decoder_1_out_5), .out_3(decoder_1_out_3),
    .in_2(_2Bit_Addr), .in_1(in_1));
  D_Latch d_latch_1 (.out_3(d_latch_1_out_3), .in_1(in_3), .in_2(and_1_out));
  and and_1 (and_1_out, decoder_1_out_3, Write);
  D_Latch d_latch_2 (.out_3(d_latch_2_out_3), .in_1(in_3), .in_2(and_2_out));
  and and_2 (and_2_out, decoder_1_out_4, Write);
  D_Latch d_latch_3 (.out_3(d_latch_3_out_3), .in_1(in_3), .in_2(and_3_out));
  and and_3 (and_3_out, decoder_1_out_5, Write);
  D_Latch d_latch_4 (.out_3(d_latch_4_out_3), .in_1(in_3), .in_2(and_4_out));
  and and_4 (and_4_out, decoder_1_out_6, Write);
  D_Latch d_latch_5 (.out_3(d_latch_5_out_3), .in_1(_3Bit_Data), .in_2(and_1_out));
  D_Latch d_latch_6 (.out_3(d_latch_6_out_3), .in_1(_3Bit_Data), .in_2(and_2_out));
  D_Latch d_latch_7 (.out_3(d_latch_7_out_3), .in_1(_3Bit_Data), .in_2(and_3_out));
  D_Latch d_latch_8 (.out_3(d_latch_8_out_3), .in_1(_3Bit_Data), .in_2(and_4_out));
  D_Latch d_latch_9 (.out_3(d_latch_9_out_3), .in_1(in_5), .in_2(and_1_out));
  D_Latch d_latch_10 (.out_3(d_latch_10_out_3), .in_1(in_5), .in_2(and_2_out));
  D_Latch d_latch_11 (.out_3(d_latch_11_out_3), .in_1(in_5), .in_2(and_3_out));
  D_Latch d_latch_12 (.out_3(d_latch_12_out_3), .in_1(in_5), .in_2(and_4_out));
  or or_1 (out_7, d_latch_1_out_3, d_latch_2_out_3, d_latch_3_out_3, d_latch_4_out_3);
  or or_2 (_3_Bit_Out, d_latch_5_out_3, d_latch_6_out_3, d_latch_7_out_3, d_latch_8_out_3);
  or or_3 (out_9, d_latch_9_out_3, d_latch_10_out_3, d_latch_11_out_3, d_latch_12_out_3);

  // Notes on the sheet:
  //   Name:
  //   Pledge:
  //   Implement  3 Bit, 4 Word RAM
  //   Nicholas Mohamed
  //   Implement the WRITE operation
  //   If you need help, look at slides 9-16 in week9.pdf
  //   The 3 Bit Output should reflect the values stored in the word selected by the 2Bit Addr
  //   I Pladge my honor that I have abided by the stevens Honor System
endmodule

module Remainder (
  input  in_1,
  input  in_2,
  input  in_3,
  input  in_4,
  input  in_5,
  output out_6,
  output out_7,
  output out_8
);

  wire and_1_out, and_2_out, and_3_out, and_4_out, and_5_out, and_6_out, and_7_out, and_8_out, not_1_out,
       not_3_out, not_4_out, not_5_out, not_6_out, not_7_out, not_8_out, not_9_out, or_1_out, or_2_out,
       or_3_out;

  and and_1 (and_1_out, in_5, in_4);
  or or_1 (or_1_out, in_5, in_4);
  not not_1 (not_1_out, in_5);
  not not_2 (out_7, or_1_out);
  and and_2 (and_2_out, not_1_out, in_4, in_3);
  and and_3 (and_3_out, in_3, not_3_out, not_4_out);
  not not_3 (not_3_out, in_2);
  not not_4 (not_4_out, in_1);
  or or_2 (or_2_out, and_6_out, and_4_out, and_3_out);
  not not_5 (not_5_out, in_3);
  and and_4 (and_4_out, not_5_out, not_6_out, in_1);
  not not_6 (not_6_out, in_2);
  and and_5 (and_5_out, and_1_out, or_2_out);
  and and_6 (and_6_out, in_3, in_2, in_1);
  not not_7 (not_7_out, in_3);
  not not_8 (not_8_out, in_1);
  and and_7 (and_7_out, not_7_out, in_2, not_8_out);
  not not_9 (not_9_out, in_2);
  and and_8 (and_8_out, in_3, not_9_out, in_1);
  or or_3 (or_3_out, and_8_out, and_7_out);
  or or_4 (out_8, and_5_out, and_2_out);
  and and_9 (out_6, and_1_out, or_3_out);

  // Notes on the sheet:
  //   Numerator
  //   Divisor
  //   Error bit (Set when division isn't possible)
  //   Part 2: Create a circuit to calculate remainders, given a 3-bit numerator and 2-bit divisor.
  //   (Hint: You may want to write a truth table first)
  //   Remainder
endmodule
